# Fritzing sketch PCB2 (saved by Fritzing 0.9.6b)
circuit board: 10.1776cm x 5.36194cm
breadboards: 1

parts:
  part = Camdenboss CTB0158-2 [part_number=CTB0158-2 package=THT]
  part_2 = Resistor [tolerance=±5% power=0.25 resistance=220 package=THT]
  part_3 = Resistor [tolerance=±5% power=0.25 resistance=220 package=THT]
  J3 = Camdenboss CTB0158-8 [part_number=CTB0158-8 package=THT]
  Part1 = Arduino Mega 2560 (Rev3)
  J4 = Camdenboss CTB0158-6 [part_number=CTB0158-6 package=THT]
  J5 = Camdenboss CTB0158-6 [part_number=CTB0158-6 package=THT]
  part_4 = Motor Driver 1A Dual TB6612FNG
  part_5 = Camdenboss CTB0158-4 [part_number=CTB0158-4 package=THT]
  part_6 = Camdenboss CTB0158-2 [part_number=CTB0158-2 package=THT]
  part_7 = Motor Driver 1A Dual TB6612FNG
  part_8 = female pin header, 1 pin [form="♀ (female)"]

nets:
  GND: part.pin1, part_2.Pin_1, part_3.Pin_0, J3.pin2, Part1.GND, J5.pin2, J5.pin5, part_4.GND, part_5.pin2, part_5.pin4, part_7.GND, part_8.pin1
  N1: part.pin2, part_4.VM, part_7.VM
  N2: part_2.Pin_0, J3.pin7, Part1.A1
  N3: part_3.Pin_1, J3.pin5, Part1.A2
  VCC: J3.pin1, J3.pin3, J3.pin6, J3.pin8, Part1.5V, J5.pin3, J5.pin4, part_4.VCC, part_4.STBY, part_5.pin1, part_5.pin3, part_7.VCC, part_7.STBY
  N4: J3.pin4, Part1.D38
  N5: Part1.A0, J5.pin6
  N6: Part1.D13_PWM, part_7.PWMA
  N7: Part1.D12_PWM, part_7.AIN2
  N8: Part1.D11_PWM, part_7.AIN1
  N9: Part1.D10_PWM, part_7.BIN1
  N10: Part1.D9_PWM, part_7.BIN2
  N11: Part1.D8_PWM, part_7.PWMB
  N12: Part1.D2_PWM, part_6.pin2
  N13: Part1.D3_PWM, part_6.pin1
  N14: Part1.D4_PWM, part_4.PWMB
  N15: Part1.D5_PWM, part_4.BIN2
  N16: Part1.D6_PWM, part_4.BIN1
  N17: Part1.D52, J5.pin1
  N18: J4.pin1, part_4.B01
  N19: J4.pin2, part_4.B02
  N20: J4.pin3, part_7.B01
  N21: J4.pin4, part_7.B02
  N22: J4.pin5, part_7.A02
  N23: J4.pin6, part_7.A01

notes:
  motor
  pwr
  +
  GND
  spinY
  spinBrn
  solR
  solK
  potR
  potG
  encA
  encB
  lift
  IR
  F1K
  F1R
  F2R
  F2K
  spin
  5V
  potY
  potB
  potO
  IR-GND
  IR-5V
  spn5V
  spnGND
  motR:
  motK:
